// Logisim project 8 Bit Computer.circ as structural Verilog: 15 circuits, main circuit main
module CPU (
  input  [7:0] ROM_Data,
  input  [7:0] Ram_Out,
  input  [7:0] ROM_Instructions,
  input  CLK,
  input  [7:0] Controller_1,
  output [7:0] _0,
  output [7:0] _1,
  output [7:0] _2,
  output [7:0] _3,
  output [7:0] _4,
  output [7:0] _5,
  output [7:0] _6,
  output [7:0] _7,
  output [7:0] RAM_Address,
  output [7:0] Ram_In,
  output RAM_CLK,
  output str,
  output sel,
  output ld,
  output [7:0] Address
);

  wire add_a_a_out, add_a_b_out, add_a_c_out, add_a_d_out, and_1_out, and_2_out, and_3_out, and_4_out,
       and_5_out, and_6_out, and_7_out, and_8_out, and_9_out, cmp_a_b_out, cmp_a_c_out, cmp_a_d_out,
       d_ff_1_q, d_ff_2_q, dec_a_out, dec_b_out, dec_c_out, dec_d_out, inc_a_out, inc_b_out, inc_c_out,
       inc_d_out, jg__a_out, jg_value_out, jmp__a_out, jmp_value_out, mov__b___d_out, mov__b__a_out,
       mov__b__c_2_out, mov__b__c_out, mov__d__a_out, mov__d__b_out, mov__d__c_out, mov_a__d_out,
       mov_a_b_out, mov_a_c_out, mov_a_d_out, mov_a_value_out, mov_b__d_out, mov_b_a_out, mov_b_c_out,
       mov_b_d_out, mov_b_value_out, mov_c__d_out, mov_c_a_out, mov_c_b_out, mov_c_d_out, mov_c_value_out,
       mov_d_a_out, mov_d_b_out, mov_d_c_out, mov_d_value_out, not_1_out, not_2_out, or_1_out, or_3_out,
       or_4_out, or_5_out, or_6_out, or_7_out, or_8_out, or_9_out, or_10_out, or_11_out, or_12_out,
       or_14_out, or_15_out, or_16_out, or_17_out, or_18_out, rea_a_out, sub_a_b_out, sub_a_c_out,
       sub_a_d_out, xor_1_out;
  wire [1:0] or_20_out;
  wire [2:0] comparator_1_greater_than, or_21_out;
  wire [5:0] jeq_value_out;
  wire [7:0] arithmatic_unit_1_out_11, led_matrix_controller_1_d_out, n8_bit_allow_1_o, n8_bit_allow_2_o,
       n8_bit_allow_3_o, n8_bit_allow_4_o, n8_bit_allow_5_o, n8_bit_allow_6_o, n8_bit_allow_7_o,
       n8_bit_allow_8_o, or_2_out, or_13_out, register_1_q, register_a_b_c_d_1_a, register_a_b_c_d_1_b,
       register_a_b_c_d_1_c, register_a_b_c_d_1_d, shifter_1_out_15, shl_c_value_2_out;

  or or_1 (or_1_out, d_ff_1_q, d_ff_1_q, d_ff_2_q, jmp_value_out, jmp__a_out);
  not not_1 (not_1_out, or_1_out);
  Counter IP (.load(or_1_out), .D(or_2_out), .count(not_1_out), .Q(Address), .clk(not_2_out));  // open: carry, clr
  not not_2 (not_2_out, CLK);
  assign or_2_out = n8_bit_allow_2_o | n8_bit_allow_3_o;  // OR_Gate or_2, 8 bits wide
  _8_bit_allow u_8_bit_allow_1 (.D(register_1_q), .A(rea_a_out), .O(n8_bit_allow_1_o));
  Register register_1 (.D(Controller_1), .en(CLK), .Q(register_1_q), .clk(CLK));  // open: clr
  and and_1 (and_1_out, comparator_1_greater_than[0], jg_value_out);
  _8_bit_allow u_8_bit_allow_2 (.D(ROM_Data), .A(d_ff_1_q), .O(n8_bit_allow_2_o));
  or or_3 (or_3_out, and_1_out, and_4_out, jmp_value_out, and_2_out, and_3_out);
  and and_2 (and_2_out, or_5_out, jeq_value_out[3]);
  and and_3 (and_3_out, jeq_value_out[0], comparator_1_greater_than[1]);
  and and_4 (and_4_out, comparator_1_greater_than[2], jeq_value_out[5]);
  D_Flip_Flop d_ff_1 (.clk(CLK), .D(or_3_out), .Q(d_ff_1_q));  // open: Qn, preset, en, reset
  _8_bit_allow u_8_bit_allow_3 (.D(register_a_b_c_d_1_a), .A(d_ff_2_q), .O(n8_bit_allow_3_o));
  and and_5 (and_5_out, jeq_value_out[1], comparator_1_greater_than[1]);
  D_Flip_Flop d_ff_2 (.clk(CLK), .D(or_4_out), .Q(d_ff_2_q));  // open: Qn, preset, en, reset
  or or_4 (or_4_out, jmp__a_out, and_5_out, and_6_out, and_7_out, and_8_out);
  and and_6 (and_6_out, jeq_value_out[2], or_5_out);
  and and_7 (and_7_out, jeq_value_out[4], comparator_1_greater_than[2]);
  and and_8 (and_8_out, jg__a_out, comparator_1_greater_than[0]);
  and mov_a__d (mov_a__d_out, ROM_Instructions[0], ~ROM_Instructions[1], ~ROM_Instructions[2], ~ROM_Instructions[3], ~ROM_Instructions[4], ~ROM_Instructions[5], ~ROM_Instructions[6], ~ROM_Instructions[7]);  // AND_Gate
  and mov_a_b (mov_a_b_out, ~ROM_Instructions[0], ROM_Instructions[1], ~ROM_Instructions[2], ~ROM_Instructions[3], ~ROM_Instructions[4], ~ROM_Instructions[5], ~ROM_Instructions[6], ~ROM_Instructions[7]);  // AND_Gate
  and mov_a_c (mov_a_c_out, ROM_Instructions[0], ROM_Instructions[1], ~ROM_Instructions[2], ~ROM_Instructions[3], ~ROM_Instructions[4], ~ROM_Instructions[5], ~ROM_Instructions[6], ~ROM_Instructions[7]);  // AND_Gate
  and mov_a_d (mov_a_d_out, ~ROM_Instructions[0], ~ROM_Instructions[1], ROM_Instructions[2], ~ROM_Instructions[3], ~ROM_Instructions[4], ~ROM_Instructions[5], ~ROM_Instructions[6], ~ROM_Instructions[7]);  // AND_Gate
  and mov_b__d (mov_b__d_out, ROM_Instructions[0], ~ROM_Instructions[1], ROM_Instructions[2], ~ROM_Instructions[3], ~ROM_Instructions[4], ~ROM_Instructions[5], ~ROM_Instructions[6], ~ROM_Instructions[7]);  // AND_Gate
  and mov_b_a (mov_b_a_out, ~ROM_Instructions[0], ROM_Instructions[1], ROM_Instructions[2], ~ROM_Instructions[3], ~ROM_Instructions[4], ~ROM_Instructions[5], ~ROM_Instructions[6], ~ROM_Instructions[7]);  // AND_Gate
  and mov_b_c (mov_b_c_out, ROM_Instructions[0], ROM_Instructions[1], ROM_Instructions[2], ~ROM_Instructions[3], ~ROM_Instructions[4], ~ROM_Instructions[5], ~ROM_Instructions[6], ~ROM_Instructions[7]);  // AND_Gate
  and mov_b_d (mov_b_d_out, ~ROM_Instructions[0], ~ROM_Instructions[1], ~ROM_Instructions[2], ROM_Instructions[3], ~ROM_Instructions[4], ~ROM_Instructions[5], ~ROM_Instructions[6], ~ROM_Instructions[7]);  // AND_Gate
  and mov_c__d (mov_c__d_out, ROM_Instructions[0], ~ROM_Instructions[1], ~ROM_Instructions[2], ROM_Instructions[3], ~ROM_Instructions[4], ~ROM_Instructions[5], ~ROM_Instructions[6], ~ROM_Instructions[7]);  // AND_Gate
  and mov_c_a (mov_c_a_out, ~ROM_Instructions[0], ROM_Instructions[1], ~ROM_Instructions[2], ROM_Instructions[3], ~ROM_Instructions[4], ~ROM_Instructions[5], ~ROM_Instructions[6], ~ROM_Instructions[7]);  // AND_Gate
  and mov_c_b (mov_c_b_out, ROM_Instructions[0], ROM_Instructions[1], ~ROM_Instructions[2], ROM_Instructions[3], ~ROM_Instructions[4], ~ROM_Instructions[5], ~ROM_Instructions[6], ~ROM_Instructions[7]);  // AND_Gate
  and mov_c_d (mov_c_d_out, ~ROM_Instructions[0], ~ROM_Instructions[1], ROM_Instructions[2], ROM_Instructions[3], ~ROM_Instructions[4], ~ROM_Instructions[5], ~ROM_Instructions[6], ~ROM_Instructions[7]);  // AND_Gate
  and mov_d_a (mov_d_a_out, ROM_Instructions[0], ~ROM_Instructions[1], ROM_Instructions[2], ROM_Instructions[3], ~ROM_Instructions[4], ~ROM_Instructions[5], ~ROM_Instructions[6], ~ROM_Instructions[7]);  // AND_Gate
  and mov_d_b (mov_d_b_out, ~ROM_Instructions[0], ROM_Instructions[1], ROM_Instructions[2], ROM_Instructions[3], ~ROM_Instructions[4], ~ROM_Instructions[5], ~ROM_Instructions[6], ~ROM_Instructions[7]);  // AND_Gate
  and mov_d_c (mov_d_c_out, ROM_Instructions[0], ROM_Instructions[1], ROM_Instructions[2], ROM_Instructions[3], ~ROM_Instructions[4], ~ROM_Instructions[5], ~ROM_Instructions[6], ~ROM_Instructions[7]);  // AND_Gate
  and mov__d__a (mov__d__a_out, ~ROM_Instructions[0], ~ROM_Instructions[1], ~ROM_Instructions[2], ~ROM_Instructions[3], ROM_Instructions[4], ~ROM_Instructions[5], ~ROM_Instructions[6], ~ROM_Instructions[7]);  // AND_Gate
  and mov__d__b (mov__d__b_out, ROM_Instructions[0], ~ROM_Instructions[1], ~ROM_Instructions[2], ~ROM_Instructions[3], ROM_Instructions[4], ~ROM_Instructions[5], ~ROM_Instructions[6], ~ROM_Instructions[7]);  // AND_Gate
  and mov__d__c (mov__d__c_out, ~ROM_Instructions[0], ROM_Instructions[1], ~ROM_Instructions[2], ~ROM_Instructions[3], ROM_Instructions[4], ~ROM_Instructions[5], ~ROM_Instructions[6], ~ROM_Instructions[7]);  // AND_Gate
  and add_a_a (add_a_a_out, ROM_Instructions[0], ROM_Instructions[1], ~ROM_Instructions[2], ~ROM_Instructions[3], ROM_Instructions[4], ~ROM_Instructions[5], ~ROM_Instructions[6], ~ROM_Instructions[7]);  // AND_Gate
  and add_a_b (add_a_b_out, ~ROM_Instructions[0], ~ROM_Instructions[1], ROM_Instructions[2], ~ROM_Instructions[3], ROM_Instructions[4], ~ROM_Instructions[5], ~ROM_Instructions[6], ~ROM_Instructions[7]);  // AND_Gate
  and add_a_c (add_a_c_out, ROM_Instructions[0], ~ROM_Instructions[1], ROM_Instructions[2], ~ROM_Instructions[3], ROM_Instructions[4], ~ROM_Instructions[5], ~ROM_Instructions[6], ~ROM_Instructions[7]);  // AND_Gate
  and add_a_d (add_a_d_out, ~ROM_Instructions[0], ROM_Instructions[1], ROM_Instructions[2], ~ROM_Instructions[3], ROM_Instructions[4], ~ROM_Instructions[5], ~ROM_Instructions[6], ~ROM_Instructions[7]);  // AND_Gate
  and mov_a_value (mov_a_value_out, ROM_Instructions[0], ROM_Instructions[1], ROM_Instructions[2], ~ROM_Instructions[3], ROM_Instructions[4], ~ROM_Instructions[5], ~ROM_Instructions[6], ~ROM_Instructions[7]);  // AND_Gate
  and mov_b_value (mov_b_value_out, ~ROM_Instructions[0], ~ROM_Instructions[1], ~ROM_Instructions[2], ROM_Instructions[3], ROM_Instructions[4], ~ROM_Instructions[5], ~ROM_Instructions[6], ~ROM_Instructions[7]);  // AND_Gate
  and mov_c_value (mov_c_value_out, ROM_Instructions[0], ~ROM_Instructions[1], ~ROM_Instructions[2], ROM_Instructions[3], ROM_Instructions[4], ~ROM_Instructions[5], ~ROM_Instructions[6], ~ROM_Instructions[7]);  // AND_Gate
  and mov_d_value (mov_d_value_out, ~ROM_Instructions[0], ROM_Instructions[1], ~ROM_Instructions[2], ROM_Instructions[3], ROM_Instructions[4], ~ROM_Instructions[5], ~ROM_Instructions[6], ~ROM_Instructions[7]);  // AND_Gate
  and sub_a_b (sub_a_b_out, ROM_Instructions[0], ROM_Instructions[1], ~ROM_Instructions[2], ROM_Instructions[3], ROM_Instructions[4], ~ROM_Instructions[5], ~ROM_Instructions[6], ~ROM_Instructions[7]);  // AND_Gate
  and sub_a_c (sub_a_c_out, ~ROM_Instructions[0], ~ROM_Instructions[1], ROM_Instructions[2], ROM_Instructions[3], ROM_Instructions[4], ~ROM_Instructions[5], ~ROM_Instructions[6], ~ROM_Instructions[7]);  // AND_Gate
  and sub_a_d (sub_a_d_out, ROM_Instructions[0], ~ROM_Instructions[1], ROM_Instructions[2], ROM_Instructions[3], ROM_Instructions[4], ~ROM_Instructions[5], ~ROM_Instructions[6], ~ROM_Instructions[7]);  // AND_Gate
  and cmp_a_b (cmp_a_b_out, ~ROM_Instructions[0], ROM_Instructions[1], ROM_Instructions[2], ROM_Instructions[3], ROM_Instructions[4], ~ROM_Instructions[5], ~ROM_Instructions[6], ~ROM_Instructions[7]);  // AND_Gate
  and cmp_a_c (cmp_a_c_out, ROM_Instructions[0], ROM_Instructions[1], ROM_Instructions[2], ROM_Instructions[3], ROM_Instructions[4], ~ROM_Instructions[5], ~ROM_Instructions[6], ~ROM_Instructions[7]);  // AND_Gate
  and cmp_a_d (cmp_a_d_out, ~ROM_Instructions[0], ~ROM_Instructions[1], ~ROM_Instructions[2], ~ROM_Instructions[3], ~ROM_Instructions[4], ROM_Instructions[5], ~ROM_Instructions[6], ~ROM_Instructions[7]);  // AND_Gate
  and jmp__a (jmp__a_out, ~ROM_Instructions[0], ROM_Instructions[1], ~ROM_Instructions[2], ROM_Instructions[3], ~ROM_Instructions[4], ROM_Instructions[5], ~ROM_Instructions[6], ~ROM_Instructions[7]);  // AND_Gate
  and jmp_value (jmp_value_out, ROM_Instructions[0], ROM_Instructions[1], ~ROM_Instructions[2], ROM_Instructions[3], ~ROM_Instructions[4], ROM_Instructions[5], ~ROM_Instructions[6], ~ROM_Instructions[7]);  // AND_Gate
  and jeq_value (jeq_value_out[0], ~ROM_Instructions[0], ~ROM_Instructions[1], ROM_Instructions[2], ROM_Instructions[3], ~ROM_Instructions[4], ROM_Instructions[5], ~ROM_Instructions[6], ~ROM_Instructions[7]);  // AND_Gate
  and jeq__a (jeq_value_out[1], ROM_Instructions[0], ~ROM_Instructions[1], ROM_Instructions[2], ROM_Instructions[3], ~ROM_Instructions[4], ROM_Instructions[5], ~ROM_Instructions[6], ~ROM_Instructions[7]);  // AND_Gate
  and jne__a (jeq_value_out[2], ~ROM_Instructions[0], ROM_Instructions[1], ROM_Instructions[2], ROM_Instructions[3], ~ROM_Instructions[4], ROM_Instructions[5], ~ROM_Instructions[6], ~ROM_Instructions[7]);  // AND_Gate
  and jne_value (jeq_value_out[3], ROM_Instructions[0], ROM_Instructions[1], ROM_Instructions[2], ROM_Instructions[3], ~ROM_Instructions[4], ROM_Instructions[5], ~ROM_Instructions[6], ~ROM_Instructions[7]);  // AND_Gate
  and jl__a (jeq_value_out[4], ~ROM_Instructions[0], ~ROM_Instructions[1], ~ROM_Instructions[2], ~ROM_Instructions[3], ROM_Instructions[4], ROM_Instructions[5], ~ROM_Instructions[6], ~ROM_Instructions[7]);  // AND_Gate
  and jl_value (jeq_value_out[5], ROM_Instructions[0], ~ROM_Instructions[1], ~ROM_Instructions[2], ~ROM_Instructions[3], ROM_Instructions[4], ROM_Instructions[5], ~ROM_Instructions[6], ~ROM_Instructions[7]);  // AND_Gate
  and jg__a (jg__a_out, ~ROM_Instructions[0], ROM_Instructions[1], ~ROM_Instructions[2], ~ROM_Instructions[3], ROM_Instructions[4], ROM_Instructions[5], ~ROM_Instructions[6], ~ROM_Instructions[7]);  // AND_Gate
  and jg_value (jg_value_out, ROM_Instructions[0], ROM_Instructions[1], ~ROM_Instructions[2], ~ROM_Instructions[3], ROM_Instructions[4], ROM_Instructions[5], ~ROM_Instructions[6], ~ROM_Instructions[7]);  // AND_Gate
  and mov__b___d (mov__b___d_out, ~ROM_Instructions[0], ~ROM_Instructions[1], ROM_Instructions[2], ~ROM_Instructions[3], ROM_Instructions[4], ROM_Instructions[5], ~ROM_Instructions[6], ~ROM_Instructions[7]);  // AND_Gate
  and mov__b__a (mov__b__a_out, ROM_Instructions[0], ~ROM_Instructions[1], ROM_Instructions[2], ~ROM_Instructions[3], ROM_Instructions[4], ROM_Instructions[5], ~ROM_Instructions[6], ~ROM_Instructions[7]);  // AND_Gate
  and mov__b__c (mov__b__c_out, ~ROM_Instructions[0], ROM_Instructions[1], ROM_Instructions[2], ~ROM_Instructions[3], ROM_Instructions[4], ROM_Instructions[5], ~ROM_Instructions[6], ~ROM_Instructions[7]);  // AND_Gate
  and mov__b__c_2 (mov__b__c_2_out, ~ROM_Instructions[0], ~ROM_Instructions[1], ~ROM_Instructions[2], ROM_Instructions[3], ROM_Instructions[4], ROM_Instructions[5], ~ROM_Instructions[6], ~ROM_Instructions[7]);  // AND_Gate
  and inc_a (inc_a_out, ROM_Instructions[0], ~ROM_Instructions[1], ~ROM_Instructions[2], ROM_Instructions[3], ROM_Instructions[4], ROM_Instructions[5], ~ROM_Instructions[6], ~ROM_Instructions[7]);  // AND_Gate
  and inc_b (inc_b_out, ~ROM_Instructions[0], ROM_Instructions[1], ~ROM_Instructions[2], ROM_Instructions[3], ROM_Instructions[4], ROM_Instructions[5], ~ROM_Instructions[6], ~ROM_Instructions[7]);  // AND_Gate
  and inc_c (inc_c_out, ROM_Instructions[0], ROM_Instructions[1], ~ROM_Instructions[2], ROM_Instructions[3], ROM_Instructions[4], ROM_Instructions[5], ~ROM_Instructions[6], ~ROM_Instructions[7]);  // AND_Gate
  and inc_d (inc_d_out, ~ROM_Instructions[0], ~ROM_Instructions[1], ROM_Instructions[2], ROM_Instructions[3], ROM_Instructions[4], ROM_Instructions[5], ~ROM_Instructions[6], ~ROM_Instructions[7]);  // AND_Gate
  and dec_a (dec_a_out, ROM_Instructions[0], ~ROM_Instructions[1], ROM_Instructions[2], ROM_Instructions[3], ROM_Instructions[4], ROM_Instructions[5], ~ROM_Instructions[6], ~ROM_Instructions[7]);  // AND_Gate
  and dec_b (dec_b_out, ~ROM_Instructions[0], ROM_Instructions[1], ROM_Instructions[2], ROM_Instructions[3], ROM_Instructions[4], ROM_Instructions[5], ~ROM_Instructions[6], ~ROM_Instructions[7]);  // AND_Gate
  and dec_c (dec_c_out, ROM_Instructions[0], ROM_Instructions[1], ROM_Instructions[2], ROM_Instructions[3], ROM_Instructions[4], ROM_Instructions[5], ~ROM_Instructions[6], ~ROM_Instructions[7]);  // AND_Gate
  and dec_d (dec_d_out, ~ROM_Instructions[0], ~ROM_Instructions[1], ~ROM_Instructions[2], ~ROM_Instructions[3], ~ROM_Instructions[4], ~ROM_Instructions[5], ROM_Instructions[6], ~ROM_Instructions[7]);  // AND_Gate
  and shr_a_value (shl_c_value_2_out[7], ROM_Instructions[0], ~ROM_Instructions[1], ~ROM_Instructions[2], ~ROM_Instructions[3], ~ROM_Instructions[4], ~ROM_Instructions[5], ROM_Instructions[6], ~ROM_Instructions[7]);  // AND_Gate
  and shr_b_value (shl_c_value_2_out[6], ~ROM_Instructions[0], ROM_Instructions[1], ~ROM_Instructions[2], ~ROM_Instructions[3], ~ROM_Instructions[4], ~ROM_Instructions[5], ROM_Instructions[6], ~ROM_Instructions[7]);  // AND_Gate
  and shr_c_value (shl_c_value_2_out[5], ROM_Instructions[0], ROM_Instructions[1], ~ROM_Instructions[2], ~ROM_Instructions[3], ~ROM_Instructions[4], ~ROM_Instructions[5], ROM_Instructions[6], ~ROM_Instructions[7]);  // AND_Gate
  and shr_d_value (shl_c_value_2_out[4], ~ROM_Instructions[0], ~ROM_Instructions[1], ROM_Instructions[2], ~ROM_Instructions[3], ~ROM_Instructions[4], ~ROM_Instructions[5], ROM_Instructions[6], ~ROM_Instructions[7]);  // AND_Gate
  and shl_a_value (shl_c_value_2_out[3], ROM_Instructions[0], ~ROM_Instructions[1], ROM_Instructions[2], ~ROM_Instructions[3], ~ROM_Instructions[4], ~ROM_Instructions[5], ROM_Instructions[6], ~ROM_Instructions[7]);  // AND_Gate
  and shl_b_value (shl_c_value_2_out[2], ~ROM_Instructions[0], ROM_Instructions[1], ROM_Instructions[2], ~ROM_Instructions[3], ~ROM_Instructions[4], ~ROM_Instructions[5], ROM_Instructions[6], ~ROM_Instructions[7]);  // AND_Gate
  and shl_c_value (shl_c_value_2_out[1], ROM_Instructions[0], ROM_Instructions[1], ROM_Instructions[2], ~ROM_Instructions[3], ~ROM_Instructions[4], ~ROM_Instructions[5], ROM_Instructions[6], ~ROM_Instructions[7]);  // AND_Gate
  and shl_c_value_2 (shl_c_value_2_out[0], ~ROM_Instructions[0], ~ROM_Instructions[1], ~ROM_Instructions[2], ROM_Instructions[3], ~ROM_Instructions[4], ~ROM_Instructions[5], ROM_Instructions[6], ~ROM_Instructions[7]);  // AND_Gate
  and rea_a (rea_a_out, ROM_Instructions[0], ~ROM_Instructions[1], ~ROM_Instructions[2], ROM_Instructions[3], ~ROM_Instructions[4], ~ROM_Instructions[5], ROM_Instructions[6], ~ROM_Instructions[7]);  // AND_Gate
  or or_5 (or_5_out, comparator_1_greater_than[2], comparator_1_greater_than[0]);
  or or_6 (or_6_out, mov__b__c_2_out, rea_a_out);
  or or_7 (or_7_out, or_12_out, mov_b_value_out, or_20_out[0]);
  or or_8 (or_8_out, or_6_out, or_20_out[1]);
  and and_9 (and_9_out, ~or_12_out, or_7_out);  // AND_Gate
  or or_9 (or_9_out, or_10_out, or_21_out[1]);
  or or_10 (or_10_out, mov_a_value_out, mov_b_value_out, or_21_out[0], or_21_out[1]);
  xor xor_1 (xor_1_out, or_12_out, mov_a_value_out);
  or or_11 (or_11_out, or_15_out, or_8_out, or_12_out);
  or or_12 (or_12_out, add_a_a_out, add_a_b_out, add_a_c_out, add_a_d_out, mov_a_value_out);
  _8_bit_allow u_8_bit_allow_4 (.D(shifter_1_out_15), .A(or_21_out[2]), .O(n8_bit_allow_4_o));
  _8_bit_allow u_8_bit_allow_5 (.D(led_matrix_controller_1_d_out), .A(mov__b__c_2_out), .O(n8_bit_allow_5_o));
  _8_bit_allow u_8_bit_allow_6 (.D(ROM_Data), .A(or_9_out), .O(n8_bit_allow_6_o));
  assign or_13_out = n8_bit_allow_6_o | n8_bit_allow_5_o | n8_bit_allow_1_o | n8_bit_allow_4_o | n8_bit_allow_7_o;  // OR_Gate or_13, 8 bits wide
  Register_A_B_C_D register_a_b_c_d_1 (
    .Data_Data_IN(n8_bit_allow_8_o), .CLK(CLK), .mov_a__d(mov_a__d_out), .mov_b__d(mov_b__d_out),
    .mov_c__d(mov_c__d_out), .mov_a_b(mov_a_b_out), .mov_a_c(mov_a_c_out), .mov_a_d(mov_a_d_out),
    .mov_b_a(mov_b_a_out), .mov_b_c(mov_b_c_out), .mov_b_d(mov_b_d_out), .mov_c_a(mov_c_a_out),
    .mov_c_b(mov_c_b_out), .mov_c_d(mov_c_d_out), .mov_d_a(mov_d_a_out), .mov_d_b(mov_d_b_out),
    .mov_d_c(mov_d_c_out), .Data_Address(RAM_Address), .Load(ld), .SEL(sel), .Data_Data_OUT(Ram_In),
    .mov__d__a(mov__d__a_out), .mov__d__b(mov__d__b_out), .mov__d__c(mov__d__c_out), .bring_a_dIn(or_11_out),
    .dIn(or_13_out), .bring_b_dIn(and_9_out), .bring_c_dIn(or_21_out[0]), .bring_d_dIn(or_21_out[1]),
    .A(register_a_b_c_d_1_a), .B(register_a_b_c_d_1_b), .C(register_a_b_c_d_1_c), .D(register_a_b_c_d_1_d),
    .mov__b__d(mov__b___d_out), .inc_a(inc_a_out), .inc_b(inc_b_out), .inc_c(inc_c_out), .inc_d(inc_d_out),
    .dec_a(dec_a_out), .dec_b(dec_b_out), .dec_c(dec_c_out), .dec_d(dec_d_out));
  or or_14 (or_14_out, or_15_out, xor_1_out);
  _8_bit_allow u_8_bit_allow_7 (.D(arithmatic_unit_1_out_11), .A(or_14_out), .O(n8_bit_allow_7_o));
  not not_3 (str, ld);
  or or_15 (or_15_out, sub_a_d_out, sub_a_c_out, sub_a_b_out);
  _8_bit_allow u_8_bit_allow_8 (.D(Ram_Out), .A(ld), .O(n8_bit_allow_8_o));
  or or_16 (or_16_out, add_a_b_out, sub_a_b_out);
  or or_17 (or_17_out, add_a_c_out, sub_a_c_out);
  LED_Matrix_controller led_matrix_controller_1 (
    .CLK(CLK), .A(register_a_b_c_d_1_a), .C(register_a_b_c_d_1_c), .D(register_a_b_c_d_1_d),
    .D_in(n8_bit_allow_8_o), .B(register_a_b_c_d_1_b), .mov__b___d(mov__b___d_out),
    .mov__b__a(mov__b__a_out), .mov__b__c(mov__b__c_out), .mov__b__d(1'b0),
    .D_out(led_matrix_controller_1_d_out), ._0(_0), ._1(_1), ._2(_2), ._3(_3), ._4(_4), ._5(_5), ._6(_6),
    ._7(_7));
  or or_18 (or_18_out, add_a_d_out, sub_a_d_out);
  DotMatrix #(.matrixcols(8), .matrixrows(8)) dotmatrix_1 (
    .col0(_0), .col1(_1), .col2(_2), .col3(_3), .col4(_4), .col5(_5), .col6(_6), .col7(_7));
  Arithmatic_unit arithmatic_unit_1 (
    .A(register_a_b_c_d_1_a), .B(register_a_b_c_d_1_b), .C(register_a_b_c_d_1_c), .D(register_a_b_c_d_1_d),
    .CLK(CLK), .Add_Sub(or_15_out), .add_a_a(add_a_a_out), .add_a_b(or_16_out), .add_a_c(or_17_out),
    .add_a_d(or_18_out), .out_11(arithmatic_unit_1_out_11));
  Comparator comparator_1 (
    .A(register_a_b_c_d_1_a), .B(register_a_b_c_d_1_b), .C(register_a_b_c_d_1_c), .D(register_a_b_c_d_1_d),
    .cmp_a_b(cmp_a_b_out), .cmp_a_c(cmp_a_c_out), .cmp_a_d(cmp_a_d_out), .CLK(CLK),
    .Greater_Than(comparator_1_greater_than[0]), .Equal(comparator_1_greater_than[1]),
    .Less_Than(comparator_1_greater_than[2]));
  or or_19 (or_20_out[1], shl_c_value_2_out[7], shl_c_value_2_out[3]);
  or or_20 (or_20_out[0], shl_c_value_2_out[6], shl_c_value_2_out[2]);
  or or_21 (or_21_out[0], shl_c_value_2_out[5], mov_c_value_out, shl_c_value_2_out[1]);
  or or_22 (or_21_out[1], shl_c_value_2_out[4], mov_d_value_out, shl_c_value_2_out[0]);
  Shifter shifter_1 (
    .A(register_a_b_c_d_1_a), .B(register_a_b_c_d_1_b), .C(register_a_b_c_d_1_c), .D(register_a_b_c_d_1_d),
    .Din(ROM_Data), .CLK(CLK), .out_15(shifter_1_out_15), .shr_a_value(shl_c_value_2_out[7]),
    .shr_b_value(shl_c_value_2_out[6]), .shr_c_value(shl_c_value_2_out[5]),
    .shr_d_value(shl_c_value_2_out[4]), .shl_a_value(shl_c_value_2_out[3]),
    .shl_b_value(shl_c_value_2_out[2]), .shl_c_value(shl_c_value_2_out[1]), .shl_d_value(shl_c_value_2_out[0]));
  or or_23 (or_21_out[2], or_20_out[1], or_20_out[0], or_21_out[0], or_21_out[1]);

  assign RAM_CLK = CLK;
endmodule

module Register_A_B_C_D (
  input  [7:0] Data_Data_IN,
  input  mov__b__d,
  input  CLK,
  input  mov_a__d,
  input  mov_b__d,
  input  mov_c__d,
  input  mov__d__a,
  input  mov__d__b,
  input  mov__d__c,
  input  mov_a_b,
  input  mov_a_c,
  input  mov_a_d,
  input  bring_a_dIn,
  input  [7:0] dIn,
  input  mov_b_a,
  input  mov_b_c,
  input  mov_b_d,
  input  bring_b_dIn,
  input  mov_c_a,
  input  mov_c_b,
  input  mov_c_d,
  input  bring_c_dIn,
  input  mov_d_a,
  input  mov_d_b,
  input  mov_d_c,
  input  bring_d_dIn,
  input  inc_a,
  input  inc_b,
  input  inc_c,
  input  inc_d,
  input  dec_a,
  input  dec_b,
  input  dec_c,
  input  dec_d,
  output [7:0] Data_Address,
  output [7:0] Data_Data_OUT,
  output Load,
  output SEL,
  output [7:0] A,
  output [7:0] B,
  output [7:0] C,
  output [7:0] D
);

  wire and_1_out, and_2_out, and_3_out, and_4_out, or_3_out, or_4_out, or_5_out, or_6_out, or_7_out,
       or_8_out, or_9_out, or_10_out, or_11_out, or_12_out, or_13_out, or_14_out, or_15_out, or_16_out,
       or_17_out, register_or_interface_4_4_1_e, register_or_interface_5_5_1_enable,
       register_or_interface_5_5_2_enable, register_or_interface_5_5_3_enable;
  wire [7:0] register_or_interface_4_4_1_d, register_or_interface_5_5_1_data,
       register_or_interface_5_5_2_data, register_or_interface_5_5_3_data;

  or or_1 (Load, mov__b__d, or_5_out);
  or or_2 (SEL, mov__b__d, or_7_out);
  or or_3 (or_3_out, bring_a_dIn, inc_a);
  or or_4 (or_4_out, bring_b_dIn, inc_b);
  or or_5 (or_5_out, mov_a__d, mov_b__d, mov_c__d);
  or or_6 (or_6_out, bring_c_dIn, inc_c);
  or or_7 (or_7_out, or_5_out, mov__d__a, mov__d__b, mov__d__c);
  or or_8 (or_8_out, bring_d_dIn, inc_d);
  RAM ram_1 (.sel(or_7_out), .clk(CLK), .ld(or_5_out));  // open: addr, data, clr
  or or_9 (or_9_out, and_3_out, dec_c);
  Register_Or_Interface_5_5 register_or_interface_5_5_1 (
    .D0(Data_Data_IN), .D1(B), .D2(C), .D3(D), .D4(dIn), .E0(mov_a__d), .E1(mov_a_b), .E2(mov_a_c),
    .E3(mov_a_d), .E4(or_3_out), .Data(register_or_interface_5_5_1_data),
    .Enable(register_or_interface_5_5_1_enable));
  and and_1 (and_1_out, register_or_interface_5_5_1_enable, ~or_13_out);  // AND_Gate
  or or_10 (or_10_out, and_1_out, dec_a);
  Register_Or_Interface_5_5 register_or_interface_5_5_2 (
    .D0(Data_Data_IN), .D1(A), .D2(C), .D3(D), .D4(dIn), .E0(mov_b__d), .E1(mov_b_a), .E2(mov_b_c),
    .E3(mov_b_d), .E4(or_4_out), .Data(register_or_interface_5_5_2_data),
    .Enable(register_or_interface_5_5_2_enable));
  and and_2 (and_2_out, register_or_interface_5_5_2_enable, ~or_15_out);  // AND_Gate
  or or_11 (or_11_out, and_2_out, dec_b);
  Register_Or_Interface_5_5 register_or_interface_5_5_3 (
    .D0(Data_Data_IN), .D1(A), .D2(B), .D3(D), .D4(dIn), .E0(mov_c__d), .E1(mov_c_a), .E2(mov_c_b),
    .E3(mov_c_d), .E4(or_6_out), .Data(register_or_interface_5_5_3_data),
    .Enable(register_or_interface_5_5_3_enable));
  and and_3 (and_3_out, register_or_interface_5_5_3_enable, ~or_16_out);  // AND_Gate
  Register_Or_Interface_4_4 register_or_interface_4_4_1 (
    .D0(A), .D1(B), .D2(C), .D3(dIn), .E0(mov_d_a), .E1(mov_d_b), .E2(mov_d_c), .E3(or_8_out),
    .D(register_or_interface_4_4_1_d), .E(register_or_interface_4_4_1_e));
  and and_4 (and_4_out, register_or_interface_4_4_1_e, ~or_14_out);  // AND_Gate
  or or_12 (or_12_out, and_4_out, dec_d);
  Register_Or_Interface_3_3 register_or_interface_3_3_1 (
    .D0(A), .D1(B), .D2(C), .E0(mov__d__a), .E1(mov__d__b), .E2(mov__d__c), .D(Data_Data_OUT));  // open: E
  Counter counter_1 (
    .load(or_10_out), .D(register_or_interface_5_5_1_data), .count(or_13_out), .Q(A), .clk(CLK));  // open: carry, clr
  or or_13 (or_13_out, inc_a, dec_a);
  Counter u_B (
    .load(or_11_out), .D(register_or_interface_5_5_2_data), .count(or_15_out), .Q(B), .clk(CLK));  // open: carry, clr
  Counter u_C (
    .load(or_9_out), .D(register_or_interface_5_5_3_data), .count(or_16_out), .Q(C), .clk(CLK));  // open: carry, clr
  Counter u_D (
    .load(or_12_out), .D(register_or_interface_4_4_1_d), .count(or_14_out), .Q(D), .clk(CLK));  // open: carry, clr
  or or_14 (or_14_out, dec_d, inc_d);
  or or_15 (or_15_out, inc_b, dec_b);
  or or_16 (or_16_out, inc_c, dec_c);
  or or_17 (or_17_out, or_7_out, mov_c__d, mov_b__d, mov_a__d, mov__b__d);
  _8_bit_allow u_8_bit_allow_1 (.D(D), .A(or_17_out), .O(Data_Address));
endmodule

module _8_bit_allow (
  input  [7:0] D,
  input  A,
  output [7:0] O
);

  and and_1 (O[0], D[0], A);
  and and_2 (O[1], D[1], A);
  and and_3 (O[2], D[2], A);
  and and_4 (O[3], D[3], A);
  and and_5 (O[4], D[4], A);
  and and_6 (O[5], D[5], A);
  and and_7 (O[6], D[6], A);
  and and_8 (O[7], D[7], A);
endmodule

module Register_or_interface_8_8 (
  input  [7:0] D0,
  input  [7:0] D1,
  input  [7:0] D2,
  input  [7:0] D3,
  input  [7:0] D4,
  input  [7:0] D5,
  input  [7:0] D6,
  input  [7:0] D7,
  input  E0,
  input  E1,
  input  E2,
  input  E3,
  input  E4,
  input  E5,
  input  E6,
  input  E7,
  output [7:0] Data,
  output Enable
);

  wire [7:0] n8_bit_allow_1_o, n8_bit_allow_2_o, n8_bit_allow_3_o, n8_bit_allow_4_o, n8_bit_allow_5_o,
       n8_bit_allow_6_o, n8_bit_allow_7_o, n8_bit_allow_8_o;

  _8_bit_allow u_8_bit_allow_1 (.D(D0), .A(E0), .O(n8_bit_allow_1_o));
  _8_bit_allow u_8_bit_allow_2 (.D(D1), .A(E1), .O(n8_bit_allow_2_o));
  _8_bit_allow u_8_bit_allow_3 (.D(D2), .A(E2), .O(n8_bit_allow_3_o));
  _8_bit_allow u_8_bit_allow_4 (.D(D3), .A(E3), .O(n8_bit_allow_4_o));
  _8_bit_allow u_8_bit_allow_5 (.D(D4), .A(E4), .O(n8_bit_allow_5_o));
  _8_bit_allow u_8_bit_allow_6 (.D(D5), .A(E5), .O(n8_bit_allow_6_o));
  _8_bit_allow u_8_bit_allow_7 (.D(D6), .A(E6), .O(n8_bit_allow_7_o));
  _8_bit_allow u_8_bit_allow_8 (.D(D7), .A(E7), .O(n8_bit_allow_8_o));
  assign Data = n8_bit_allow_1_o | n8_bit_allow_2_o | n8_bit_allow_3_o | n8_bit_allow_4_o | n8_bit_allow_5_o | n8_bit_allow_6_o | n8_bit_allow_7_o | n8_bit_allow_8_o;  // OR_Gate or_1, 8 bits wide
  or or_2 (Enable, E0, E1, E2, E3, E4, E5, E6, E7);
endmodule

module Register_Or_Interface_3_3 (
  input  [7:0] D0,
  input  [7:0] D1,
  input  [7:0] D2,
  input  E0,
  input  E1,
  input  E2,
  output [7:0] D,
  output E
);

  wire [7:0] n8_bit_allow_1_o, n8_bit_allow_2_o, n8_bit_allow_3_o;

  _8_bit_allow u_8_bit_allow_1 (.D(D0), .A(E0), .O(n8_bit_allow_1_o));
  _8_bit_allow u_8_bit_allow_2 (.D(D1), .A(E1), .O(n8_bit_allow_2_o));
  _8_bit_allow u_8_bit_allow_3 (.D(D2), .A(E2), .O(n8_bit_allow_3_o));
  assign D = n8_bit_allow_1_o | n8_bit_allow_2_o | n8_bit_allow_3_o;  // OR_Gate or_1, 8 bits wide
  or or_2 (E, E0, E1, E2);
endmodule

module Register_Or_Interface_4_4 (
  input  [7:0] D0,
  input  [7:0] D1,
  input  [7:0] D2,
  input  [7:0] D3,
  input  E0,
  input  E1,
  input  E2,
  input  E3,
  output [7:0] D,
  output E
);

  wire and_1_out, and_2_out, and_3_out;
  wire [7:0] n8_bit_allow_1_o, n8_bit_allow_2_o, n8_bit_allow_3_o, n8_bit_allow_4_o;

  and and_1 (and_1_out, E0, ~E3);  // AND_Gate
  and and_2 (and_2_out, E1, ~E3);  // AND_Gate
  and and_3 (and_3_out, E2, ~E3);  // AND_Gate
  _8_bit_allow u_8_bit_allow_1 (.D(D0), .A(and_1_out), .O(n8_bit_allow_1_o));
  _8_bit_allow u_8_bit_allow_2 (.D(D1), .A(and_2_out), .O(n8_bit_allow_2_o));
  _8_bit_allow u_8_bit_allow_3 (.D(D2), .A(and_3_out), .O(n8_bit_allow_3_o));
  _8_bit_allow u_8_bit_allow_4 (.D(D3), .A(E3), .O(n8_bit_allow_4_o));
  assign D = n8_bit_allow_1_o | n8_bit_allow_2_o | n8_bit_allow_3_o | n8_bit_allow_4_o;  // OR_Gate or_1, 8 bits wide
  or or_2 (E, E0, E1, E2, E3);
endmodule

module Register_Or_Interface_5_5 (
  input  [7:0] D0,
  input  [7:0] D1,
  input  [7:0] D2,
  input  [7:0] D3,
  input  [7:0] D4,
  input  E0,
  input  E1,
  input  E2,
  input  E3,
  input  E4,
  output [7:0] Data,
  output Enable
);

  wire and_1_out, and_2_out, and_3_out, and_4_out;
  wire [7:0] n8_bit_allow_1_o, n8_bit_allow_2_o, n8_bit_allow_3_o, n8_bit_allow_4_o, n8_bit_allow_5_o;

  and and_1 (and_1_out, E0, ~E4);  // AND_Gate
  and and_2 (and_2_out, E1, ~E4);  // AND_Gate
  and and_3 (and_3_out, E2, ~E4);  // AND_Gate
  and and_4 (and_4_out, E3, ~E4);  // AND_Gate
  _8_bit_allow u_8_bit_allow_1 (.D(D0), .A(and_1_out), .O(n8_bit_allow_1_o));
  _8_bit_allow u_8_bit_allow_2 (.D(D1), .A(and_2_out), .O(n8_bit_allow_2_o));
  _8_bit_allow u_8_bit_allow_3 (.D(D2), .A(and_3_out), .O(n8_bit_allow_3_o));
  _8_bit_allow u_8_bit_allow_4 (.D(D3), .A(and_4_out), .O(n8_bit_allow_4_o));
  _8_bit_allow u_8_bit_allow_5 (.D(D4), .A(E4), .O(n8_bit_allow_5_o));
  assign Data = n8_bit_allow_1_o | n8_bit_allow_2_o | n8_bit_allow_3_o | n8_bit_allow_4_o | n8_bit_allow_5_o;  // OR_Gate or_1, 8 bits wide
  or or_2 (Enable, E0, E1, E2, E3, E4);
endmodule

module Adder (
  input  [7:0] A,
  input  [7:0] B,
  input  Add_Sub,
  output [7:0] Out
);

  wire not_1_out;
  wire [7:0] adder_1_out, n8_bit_allow_1_o, n8_bit_allow_2_o, n8_bit_allow_3_o, n8_bit_allow_4_o,
       subtractor_1_out;

  not not_1 (not_1_out, Add_Sub);
  _8_bit_allow u_8_bit_allow_1 (.D(A), .A(not_1_out), .O(n8_bit_allow_1_o));
  _8_bit_allow u_8_bit_allow_2 (.D(B), .A(not_1_out), .O(n8_bit_allow_2_o));
  _8_bit_allow u_8_bit_allow_3 (.D(A), .A(Add_Sub), .O(n8_bit_allow_3_o));
  _8_bit_allow u_8_bit_allow_4 (.D(B), .A(Add_Sub), .O(n8_bit_allow_4_o));
  Adder_part adder_1 (.a(n8_bit_allow_1_o), .b(n8_bit_allow_2_o), .out(adder_1_out));  // open: cin, cout
  Subtractor subtractor_1 (.a(n8_bit_allow_3_o), .b(n8_bit_allow_4_o), .out(subtractor_1_out));  // open: bin, bout
  assign Out = adder_1_out | subtractor_1_out;  // OR_Gate or_1, 8 bits wide
endmodule

module Arithmatic_unit (
  input  [7:0] A,
  input  [7:0] B,
  input  [7:0] C,
  input  [7:0] D,
  input  CLK,
  input  Add_Sub,
  input  add_a_a,
  input  add_a_b,
  input  add_a_c,
  input  add_a_d,
  output [7:0] out_11
);

  wire [7:0] adder_1_out, n8_bit_allow_1_o, n8_bit_allow_2_o, n8_bit_allow_3_o, n8_bit_allow_4_o, or_1_out;

  _8_bit_allow u_8_bit_allow_1 (.D(A), .A(add_a_a), .O(n8_bit_allow_1_o));
  _8_bit_allow u_8_bit_allow_2 (.D(B), .A(add_a_b), .O(n8_bit_allow_2_o));
  _8_bit_allow u_8_bit_allow_3 (.D(C), .A(add_a_c), .O(n8_bit_allow_3_o));
  _8_bit_allow u_8_bit_allow_4 (.D(D), .A(add_a_d), .O(n8_bit_allow_4_o));
  assign or_1_out = n8_bit_allow_1_o | n8_bit_allow_2_o | n8_bit_allow_3_o | n8_bit_allow_4_o;  // OR_Gate or_1, 8 bits wide
  Adder adder_1 (.A(A), .B(or_1_out), .Add_Sub(Add_Sub), .Out(adder_1_out));
  Register register_1 (.D(adder_1_out), .en(CLK), .Q(out_11), .clk(CLK));  // open: clr
endmodule

module Comparator (
  input  [7:0] A,
  input  [7:0] B,
  input  [7:0] C,
  input  [7:0] D,
  input  cmp_a_b,
  input  cmp_a_c,
  input  cmp_a_d,
  input  CLK,
  output Greater_Than,
  output Equal,
  output Less_Than
);

  wire and_1_out, and_2_out, d_ff_1_qn, d_ff_2_qn, or_1_out, subtractor_1_bout, subtractor_2_bout;
  wire [7:0] n8_bit_allow_1_o, n8_bit_allow_2_o, n8_bit_allow_3_o, or_2_out, subtractor_1_out;

  _8_bit_allow u_8_bit_allow_1 (.D(B), .A(cmp_a_b), .O(n8_bit_allow_1_o));
  _8_bit_allow u_8_bit_allow_2 (.D(C), .A(cmp_a_c), .O(n8_bit_allow_2_o));
  _8_bit_allow u_8_bit_allow_3 (.D(D), .A(cmp_a_d), .O(n8_bit_allow_3_o));
  or or_1 (or_1_out, cmp_a_b, cmp_a_c, cmp_a_d);
  assign or_2_out = n8_bit_allow_1_o | n8_bit_allow_2_o | n8_bit_allow_3_o;  // OR_Gate or_2, 8 bits wide
  and and_1 (and_1_out, or_1_out, CLK);
  Subtractor subtractor_1 (.a(A), .b(or_2_out), .out(subtractor_1_out), .bout(subtractor_1_bout));  // open: bin
  Subtractor subtractor_2 (.a({8{1'b0}}), .b(subtractor_1_out), .bout(subtractor_2_bout));  // open: out, bin
  D_Flip_Flop d_ff_1 (
    .clk(and_1_out), .D(subtractor_1_bout), .Q(Less_Than), .Qn(d_ff_1_qn));  // open: preset, en, reset
  and and_2 (and_2_out, subtractor_2_bout, ~subtractor_1_bout);  // AND_Gate
  D_Flip_Flop d_ff_2 (.clk(and_1_out), .D(and_2_out), .Q(Greater_Than), .Qn(d_ff_2_qn));  // open: preset, en, reset
  and and_3 (Equal, d_ff_2_qn, d_ff_1_qn);
endmodule

module LED_Matrix_controller (
  input  CLK,
  input  [7:0] A,
  input  [7:0] C,
  input  [7:0] D,
  input  [7:0] D_in,
  input  [7:0] B,
  input  mov__b___d,
  input  mov__b__a,
  input  mov__b__c,
  input  mov__b__d,
  output [7:0] _0,
  output [7:0] _1,
  output [7:0] _2,
  output [7:0] _3,
  output [7:0] _4,
  output [7:0] _5,
  output [7:0] D_out,
  output [7:0] _6,
  output [7:0] _7
);

  wire and_1_out, or_2_out;
  wire [7:0] n8_bit_allow_1_o, n8_bit_allow_2_o, n8_bit_allow_3_o, n8_bit_allow_4_o, n8_bit_allow_5_o,
       n8_bit_allow_6_o, n8_bit_allow_7_o, n8_bit_allow_8_o, n8_bit_allow_9_o, n8_bit_allow_10_o,
       n8_bit_allow_11_o, n8_bit_allow_12_o, n8_bit_allow_13_o, or_3_out;

  assign D_out = n8_bit_allow_6_o | n8_bit_allow_7_o | n8_bit_allow_8_o | n8_bit_allow_9_o | n8_bit_allow_10_o | n8_bit_allow_11_o | n8_bit_allow_12_o | n8_bit_allow_13_o;  // OR_Gate or_1, 8 bits wide
  _8_bit_allow u_8_bit_allow_1 (.D(A), .A(mov__b__a), .O(n8_bit_allow_1_o));
  _8_bit_allow u_8_bit_allow_2 (.D(C), .A(mov__b__c), .O(n8_bit_allow_2_o));
  _8_bit_allow u_8_bit_allow_3 (.D(D), .A(mov__b__d), .O(n8_bit_allow_3_o));
  _8_bit_allow u_8_bit_allow_4 (.D(D_in), .A(mov__b___d), .O(n8_bit_allow_4_o));
  or or_2 (or_2_out, mov__b___d, mov__b__a, mov__b__c, mov__b__d);
  _8_bit_allow u_8_bit_allow_5 (.D(B), .A(or_2_out), .O(n8_bit_allow_5_o));
  _8_bit_allow u_8_bit_allow_6 (.D(_7), .A(n8_bit_allow_5_o[7]), .O(n8_bit_allow_6_o));
  _8_bit_allow u_8_bit_allow_7 (.D(_6), .A(n8_bit_allow_5_o[6]), .O(n8_bit_allow_7_o));
  _8_bit_allow u_8_bit_allow_8 (.D(_5), .A(n8_bit_allow_5_o[5]), .O(n8_bit_allow_8_o));
  _8_bit_allow u_8_bit_allow_9 (.D(_4), .A(n8_bit_allow_5_o[4]), .O(n8_bit_allow_9_o));
  _8_bit_allow u_8_bit_allow_10 (.D(_3), .A(n8_bit_allow_5_o[3]), .O(n8_bit_allow_10_o));
  _8_bit_allow u_8_bit_allow_11 (.D(_2), .A(n8_bit_allow_5_o[2]), .O(n8_bit_allow_11_o));
  _8_bit_allow u_8_bit_allow_12 (.D(_1), .A(n8_bit_allow_5_o[1]), .O(n8_bit_allow_12_o));
  _8_bit_allow u_8_bit_allow_13 (.D(_0), .A(n8_bit_allow_5_o[0]), .O(n8_bit_allow_13_o));
  assign or_3_out = n8_bit_allow_1_o | n8_bit_allow_2_o | n8_bit_allow_3_o | n8_bit_allow_4_o;  // OR_Gate or_3, 8 bits wide
  and and_1 (and_1_out, or_2_out, n8_bit_allow_5_o[0]);
  Register register_1 (.D(or_3_out), .en(and_1_out), .Q(_0), .clk(CLK));  // open: clr
  Register register_2 (.D(or_3_out), .en(n8_bit_allow_5_o[1]), .Q(_1), .clk(CLK));  // open: clr
  Register register_3 (.D(or_3_out), .en(n8_bit_allow_5_o[2]), .Q(_2), .clk(CLK));  // open: clr
  Register register_4 (.D(or_3_out), .en(n8_bit_allow_5_o[3]), .Q(_3), .clk(CLK));  // open: clr
  Register register_5 (.D(or_3_out), .en(n8_bit_allow_5_o[4]), .Q(_4), .clk(CLK));  // open: clr
  Register register_6 (.D(or_3_out), .en(n8_bit_allow_5_o[5]), .Q(_5), .clk(CLK));  // open: clr
  Register register_7 (.D(or_3_out), .en(n8_bit_allow_5_o[6]), .Q(_6), .clk(CLK));  // open: clr
  Register register_8 (.D(or_3_out), .en(n8_bit_allow_5_o[7]), .Q(_7), .clk(CLK));  // open: clr
  DotMatrix #(.matrixcols(8), .matrixrows(8)) dotmatrix_1 (
    .col0(_0), .col1(_1), .col2(_2), .col3(_3), .col4(_4), .col5(_5), .col6(_6), .col7(_7));
endmodule

module Shifter (
  input  [7:0] A,
  input  [7:0] B,
  input  [7:0] C,
  input  [7:0] D,
  input  [7:0] Din,
  input  CLK,
  input  shr_a_value,
  input  shr_b_value,
  input  shr_c_value,
  input  shr_d_value,
  input  shl_a_value,
  input  shl_b_value,
  input  shl_c_value,
  input  shl_d_value,
  output [7:0] out_15
);

  wire and_1_out, not_1_out, or_1_out, or_2_out, or_3_out, or_4_out, or_6_out, or_7_out;
  wire [7:0] n8_bit_allow_1_o, n8_bit_allow_2_o, n8_bit_allow_3_o, n8_bit_allow_4_o, n8_bit_allow_5_o,
       n8_bit_allow_6_o, or_5_out, shifter_1_out, shifter_2_out;

  or or_1 (or_1_out, shr_a_value, shl_a_value);
  or or_2 (or_2_out, shr_c_value, shl_c_value);
  or or_3 (or_3_out, shr_b_value, shl_b_value);
  _8_bit_allow u_8_bit_allow_1 (.D(A), .A(or_1_out), .O(n8_bit_allow_1_o));
  _8_bit_allow u_8_bit_allow_2 (.D(B), .A(or_3_out), .O(n8_bit_allow_2_o));
  _8_bit_allow u_8_bit_allow_3 (.D(C), .A(or_2_out), .O(n8_bit_allow_3_o));
  _8_bit_allow u_8_bit_allow_4 (.D(D), .A(or_4_out), .O(n8_bit_allow_4_o));
  or or_4 (or_4_out, shr_d_value, shl_d_value);
  assign or_5_out = n8_bit_allow_1_o | n8_bit_allow_2_o | n8_bit_allow_3_o | n8_bit_allow_4_o;  // OR_Gate or_5, 8 bits wide
  and and_1 (and_1_out, CLK, or_6_out);
  or or_6 (or_6_out, or_1_out, or_3_out, or_2_out, or_4_out);
  _8_bit_allow u_8_bit_allow_5 (.D(or_5_out), .A(not_1_out), .O(n8_bit_allow_5_o));
  Shifter_part #(.shift("lr")) shifter_1 (.in(n8_bit_allow_5_o), .\dist (Din[2:0]), .out(shifter_1_out));
  _8_bit_allow u_8_bit_allow_6 (.D(or_5_out), .A(or_7_out), .O(n8_bit_allow_6_o));
  not not_1 (not_1_out, or_7_out);
  or or_7 (or_7_out, shl_a_value, shl_b_value, shl_c_value, shl_d_value);
  Shifter_part shifter_2 (.in(n8_bit_allow_6_o), .\dist (Din[2:0]), .out(shifter_2_out));
  assign out_15 = shifter_1_out | shifter_2_out;  // OR_Gate or_8, 8 bits wide
endmodule

module main (
);

  wire clock_1_out, cpu_1_ld, cpu_1_ram_clk, cpu_1_sel, cpu_1_str;
  wire [7:0] button_8_out, cpu_1__0, cpu_1__1, cpu_1__2, cpu_1__3, cpu_1__4, cpu_1__5, cpu_1__6, cpu_1__7,
       cpu_1_address, cpu_1_ram_address, cpu_1_ram_in, ram_1_data, rom_1_data, rom_2_data;

  ROM rom_1 (.addr(cpu_1_address), .data(rom_1_data), .sel(1'b1));
  ROM rom_2 (.addr(cpu_1_address), .data(rom_2_data), .sel(1'b1));
  Button button_1 (.out(button_8_out[6]));
  Button button_2 (.out(button_8_out[7]));
  Button button_3 (.out(button_8_out[5]));
  Button button_4 (.out(button_8_out[4]));
  Button button_5 (.out(button_8_out[2]));
  Button button_6 (.out(button_8_out[3]));
  Button button_7 (.out(button_8_out[1]));
  Clock clock_1 (.out(clock_1_out));
  Button button_8 (.out(button_8_out[0]));
  CPU cpu_1 (
    ._0(cpu_1__0), ._1(cpu_1__1), ._2(cpu_1__2), ._3(cpu_1__3), ._4(cpu_1__4), ._5(cpu_1__5), ._6(cpu_1__6),
    ._7(cpu_1__7), .CLK(clock_1_out), .Address(cpu_1_address), .ROM_Data(rom_1_data),
    .ROM_Instructions(rom_2_data), .Controller_1(button_8_out), .RAM_Address(cpu_1_ram_address),
    .Ram_In(cpu_1_ram_in), .ld(cpu_1_ld), .sel(cpu_1_sel), .str(cpu_1_str), .RAM_CLK(cpu_1_ram_clk),
    .Ram_Out(ram_1_data));
  DotMatrix #(.matrixcols(8), .matrixrows(8)) dotmatrix_1 (
    .col0(cpu_1__0), .col1(cpu_1__1), .col2(cpu_1__2), .col3(cpu_1__3), .col4(cpu_1__4), .col5(cpu_1__5),
    .col6(cpu_1__6), .col7(cpu_1__7));
  RAM #(.bus("separate")) ram_1 (
    .addr(cpu_1_ram_address), .din(cpu_1_ram_in), .data(ram_1_data), .str(cpu_1_str), .sel(cpu_1_sel),
    .clk(cpu_1_ram_clk), .ld(cpu_1_ld));  // open: clr

  // Notes on the sheet:
  //   contents of rom_1 (hex, n*v repeats v):
  //   0 ff 0 1 65 7 0 0 67 16 16 4*0 68 1 4*0 40 0 1b 10 0 25 2e 65 0 e0 0 14 1 0 0 14 65 0 7 0 14 1 0 0
  //   14 66 4*0 66 0 68 0 1 0 44 0 40 1 66 0 4b 0 68 0 4b 80 0 49 1 3d 1 41 66 4*0 14
  //   contents of rom_2 (hex, n*v repeats v):
  //   17 18 35 18 1a 17 10 35 1a 17 18 35 10 40 11 1a 17 10 3c 10 49 19 1f 2c 19 1f 2c 2b 1a 1 19 1f 2c 45
  //   10 35 2b 1a 1 19 1f 2c 41 10 35 2b 1a 5 3c 1 35 1a 5 1a 9 17 1f 2c 1e 2c 46 1a 11 2b 17 1a 10 2b 17
  //   1e 2c 42 2b 17 2b 1a 5 3c 1 35 2b
endmodule

module LED_Matrix_Controller_2 (
  input  CLK,
  input  [7:0] A,
  input  [7:0] C,
  input  [7:0] d,
  input  [7:0] B,
  input  mov__b__a,
  input  mov__b__c,
  input  mov__b___d,
  input  mov_a__b,
  output [7:0] out_10
);

  wire demultiplexer_1_out0, demultiplexer_1_out1, demultiplexer_1_out2, demultiplexer_1_out3,
       demultiplexer_1_out4, demultiplexer_1_out5, demultiplexer_1_out6, demultiplexer_1_out7,
       demultiplexer_1_out8, demultiplexer_1_out9, demultiplexer_1_out10, demultiplexer_1_out11,
       demultiplexer_1_out12, demultiplexer_1_out13, demultiplexer_1_out14, demultiplexer_1_out15,
       demultiplexer_2_out0, demultiplexer_2_out1, demultiplexer_2_out2, demultiplexer_2_out3,
       demultiplexer_2_out4, demultiplexer_2_out5, demultiplexer_2_out6, demultiplexer_2_out7,
       demultiplexer_2_out8, demultiplexer_2_out9, demultiplexer_2_out10, demultiplexer_2_out11,
       demultiplexer_2_out12, demultiplexer_2_out13, demultiplexer_2_out14, demultiplexer_2_out15, not_1_out,
       not_2_out, not_3_out, or_1_out, undriven_14, undriven_15, undriven_16, undriven_17;
  wire [1:0] undriven, undriven_2, undriven_3, undriven_4, undriven_5, undriven_6, undriven_7, undriven_8,
       undriven_9, undriven_10, undriven_11, undriven_12, undriven_18, undriven_19, undriven_20, undriven_21;
  wire [7:0] counter_1_q, multiplexer_1_out, n8_bit_allow_1_o, n8_bit_allow_2_o, n8_bit_allow_3_o, or_2_out,
       undriven_13, undriven_22;
  wire [31:0] n4_registers_group_1_out, n4_registers_group_2_out, n4_registers_group_3_out,
       n4_registers_group_4_out, n4_registers_group_5_out, n4_registers_group_6_out,
       n4_registers_group_7_out, n4_registers_group_8_out, n4_registers_group_9_out,
       n4_registers_group_10_out, n4_registers_group_11_out, n4_registers_group_12_out,
       n4_registers_group_13_out, n4_registers_group_14_out, n4_registers_group_15_out,
       n4_registers_group_16_out, n4_registers_group_17_out, n4_registers_group_18_out,
       n4_registers_group_19_out, n4_registers_group_20_out, n4_registers_group_21_out,
       n4_registers_group_22_out, n4_registers_group_23_out, n4_registers_group_24_out,
       n4_registers_group_25_out, n4_registers_group_26_out, n4_registers_group_27_out,
       n4_registers_group_28_out, n4_registers_group_29_out, n4_registers_group_30_out,
       n4_registers_group_31_out, n4_registers_group_32_out;

  _8_bit_allow u_8_bit_allow_1 (.D(A), .A(mov__b__a), .O(n8_bit_allow_1_o));
  _8_bit_allow u_8_bit_allow_2 (.D(C), .A(mov__b__c), .O(n8_bit_allow_2_o));
  _8_bit_allow u_8_bit_allow_3 (.D(d), .A(mov__b___d), .O(n8_bit_allow_3_o));
  or or_1 (or_1_out, mov__b__a, mov__b__c, mov__b___d, mov_a__b);
  assign or_2_out = n8_bit_allow_1_o | n8_bit_allow_2_o | n8_bit_allow_3_o;  // OR_Gate or_2, 8 bits wide
  Multiplexer #(.width(8), .disabled(0)) multiplexer_1 (
    .in0(counter_1_q), .in1(B), .out(multiplexer_1_out), .sel(or_1_out), .en(1'b1));
  not not_1 (not_1_out, CLK);
  not not_2 (not_2_out, or_1_out);
  not not_3 (not_3_out, or_1_out);
  Counter counter_1 (.count(not_2_out), .Q(counter_1_q), .clk(not_1_out), .clr(or_1_out));  // open: load, D, carry
  RAM #(.bus("separate")) ram_1 (
    .addr(multiplexer_1_out), .din(or_2_out), .data(out_10), .str(or_1_out), .sel(1'b1), .clk(CLK),
    .ld(not_3_out));  // open: clr
  Demultiplexer #(.select(4)) demultiplexer_1 (
    .out0(demultiplexer_1_out0), .out1(demultiplexer_1_out1), .out2(demultiplexer_1_out2),
    .out3(demultiplexer_1_out3), .out4(demultiplexer_1_out4), .out5(demultiplexer_1_out5),
    .out6(demultiplexer_1_out6), .out7(demultiplexer_1_out7), .out8(demultiplexer_1_out8),
    .out9(demultiplexer_1_out9), .out10(demultiplexer_1_out10), .out11(demultiplexer_1_out11),
    .out12(demultiplexer_1_out12), .out13(demultiplexer_1_out13), .out14(demultiplexer_1_out14),
    .out15(demultiplexer_1_out15), .in(undriven_16), .sel(undriven_13[3:0]), .en(undriven_17));
  Demultiplexer #(.select(4)) demultiplexer_2 (
    .out0(demultiplexer_2_out0), .out1(demultiplexer_2_out1), .out2(demultiplexer_2_out2),
    .out3(demultiplexer_2_out3), .out4(demultiplexer_2_out4), .out5(demultiplexer_2_out5),
    .out6(demultiplexer_2_out6), .out7(demultiplexer_2_out7), .out8(demultiplexer_2_out8),
    .out9(demultiplexer_2_out9), .out10(demultiplexer_2_out10), .out11(demultiplexer_2_out11),
    .out12(demultiplexer_2_out12), .out13(demultiplexer_2_out13), .out14(demultiplexer_2_out14),
    .out15(demultiplexer_2_out15), .in(undriven_15), .sel(undriven_13[7:4]), .en(undriven_14));
  DotMatrix #(.matrixcols(32), .matrixrows(32)) dotmatrix_1 (
    .col0(n4_registers_group_1_out), .col1(n4_registers_group_2_out), .col2(n4_registers_group_3_out),
    .col3(n4_registers_group_4_out), .col4(n4_registers_group_5_out), .col5(n4_registers_group_6_out),
    .col6(n4_registers_group_7_out), .col7(n4_registers_group_8_out), .col8(n4_registers_group_9_out),
    .col9(n4_registers_group_10_out), .col10(n4_registers_group_11_out), .col11(n4_registers_group_12_out),
    .col12(n4_registers_group_13_out), .col13(n4_registers_group_14_out), .col14(n4_registers_group_15_out),
    .col15(n4_registers_group_16_out), .col16(n4_registers_group_17_out), .col17(n4_registers_group_18_out),
    .col18(n4_registers_group_19_out), .col19(n4_registers_group_20_out), .col20(n4_registers_group_21_out),
    .col21(n4_registers_group_22_out), .col22(n4_registers_group_23_out), .col23(n4_registers_group_24_out),
    .col24(n4_registers_group_25_out), .col25(n4_registers_group_26_out), .col26(n4_registers_group_27_out),
    .col27(n4_registers_group_28_out), .col28(n4_registers_group_29_out), .col29(n4_registers_group_30_out),
    .col30(n4_registers_group_31_out), .col31(n4_registers_group_32_out));
  _4_Registers_Group u_4_registers_group_1 (
    .CLK(CLK), .Data(undriven_22), .Enable(demultiplexer_1_out0), .Selector(undriven_12),
    .Out(n4_registers_group_1_out));
  _4_Registers_Group u_4_registers_group_2 (
    .CLK(CLK), .Data(undriven_22), .Enable(demultiplexer_1_out1), .Selector(undriven_11),
    .Out(n4_registers_group_2_out));
  _4_Registers_Group u_4_registers_group_3 (
    .CLK(CLK), .Data(undriven_22), .Enable(demultiplexer_1_out2), .Selector(undriven_21),
    .Out(n4_registers_group_3_out));
  _4_Registers_Group u_4_registers_group_4 (
    .CLK(CLK), .Data(undriven_22), .Enable(demultiplexer_1_out3), .Selector(undriven_10),
    .Out(n4_registers_group_4_out));
  _4_Registers_Group u_4_registers_group_5 (
    .CLK(CLK), .Data(undriven_22), .Enable(demultiplexer_1_out4), .Selector(undriven_9),
    .Out(n4_registers_group_5_out));
  _4_Registers_Group u_4_registers_group_6 (
    .CLK(CLK), .Data(undriven_22), .Enable(demultiplexer_1_out5), .Selector(undriven_8),
    .Out(n4_registers_group_6_out));
  _4_Registers_Group u_4_registers_group_7 (
    .CLK(CLK), .Data(undriven_22), .Enable(demultiplexer_1_out6), .Selector(undriven_20),
    .Out(n4_registers_group_7_out));
  _4_Registers_Group u_4_registers_group_8 (
    .CLK(CLK), .Data(undriven_22), .Enable(demultiplexer_1_out7), .Selector(undriven_19),
    .Out(n4_registers_group_8_out));
  _4_Registers_Group u_4_registers_group_9 (
    .CLK(CLK), .Data(undriven_22), .Enable(demultiplexer_1_out8), .Selector(undriven_7),
    .Out(n4_registers_group_9_out));
  _4_Registers_Group u_4_registers_group_10 (
    .CLK(CLK), .Data(undriven_22), .Enable(demultiplexer_1_out9), .Selector(undriven_6),
    .Out(n4_registers_group_10_out));
  _4_Registers_Group u_4_registers_group_11 (
    .CLK(CLK), .Data(undriven_22), .Enable(demultiplexer_1_out10), .Selector(undriven_18),
    .Out(n4_registers_group_11_out));
  _4_Registers_Group u_4_registers_group_12 (
    .CLK(CLK), .Data(undriven_22), .Enable(demultiplexer_1_out11), .Selector(undriven_5),
    .Out(n4_registers_group_12_out));
  _4_Registers_Group u_4_registers_group_13 (
    .CLK(CLK), .Data(undriven_22), .Enable(demultiplexer_1_out12), .Selector(undriven_4),
    .Out(n4_registers_group_13_out));
  _4_Registers_Group u_4_registers_group_14 (
    .CLK(CLK), .Data(undriven_22), .Enable(demultiplexer_1_out13), .Selector(undriven_3),
    .Out(n4_registers_group_14_out));
  _4_Registers_Group u_4_registers_group_15 (
    .CLK(CLK), .Data(undriven_22), .Enable(demultiplexer_1_out14), .Selector(undriven_2),
    .Out(n4_registers_group_15_out));
  _4_Registers_Group u_4_registers_group_16 (
    .CLK(CLK), .Data(undriven_22), .Enable(demultiplexer_1_out15), .Selector(undriven),
    .Out(n4_registers_group_16_out));
  _4_Registers_Group u_4_registers_group_17 (
    .CLK(CLK), .Data(undriven_22), .Enable(demultiplexer_2_out0), .Out(n4_registers_group_17_out));  // open: Selector
  _4_Registers_Group u_4_registers_group_18 (
    .CLK(CLK), .Data(undriven_22), .Enable(demultiplexer_2_out1), .Out(n4_registers_group_18_out));  // open: Selector
  _4_Registers_Group u_4_registers_group_19 (
    .CLK(CLK), .Data(undriven_22), .Enable(demultiplexer_2_out2), .Out(n4_registers_group_19_out));  // open: Selector
  _4_Registers_Group u_4_registers_group_20 (
    .CLK(CLK), .Data(undriven_22), .Enable(demultiplexer_2_out3), .Out(n4_registers_group_20_out));  // open: Selector
  _4_Registers_Group u_4_registers_group_21 (
    .CLK(CLK), .Data(undriven_22), .Enable(demultiplexer_2_out4), .Out(n4_registers_group_21_out));  // open: Selector
  _4_Registers_Group u_4_registers_group_22 (
    .CLK(CLK), .Data(undriven_22), .Enable(demultiplexer_2_out5), .Out(n4_registers_group_22_out));  // open: Selector
  _4_Registers_Group u_4_registers_group_23 (
    .CLK(CLK), .Data(undriven_22), .Enable(demultiplexer_2_out6), .Out(n4_registers_group_23_out));  // open: Selector
  _4_Registers_Group u_4_registers_group_24 (
    .CLK(CLK), .Data(undriven_22), .Enable(demultiplexer_2_out7), .Out(n4_registers_group_24_out));  // open: Selector
  _4_Registers_Group u_4_registers_group_25 (
    .CLK(CLK), .Data(undriven_22), .Enable(demultiplexer_2_out8), .Out(n4_registers_group_25_out));  // open: Selector
  _4_Registers_Group u_4_registers_group_26 (
    .CLK(CLK), .Data(undriven_22), .Enable(demultiplexer_2_out9), .Out(n4_registers_group_26_out));  // open: Selector
  _4_Registers_Group u_4_registers_group_27 (
    .CLK(CLK), .Data(undriven_22), .Enable(demultiplexer_2_out10), .Out(n4_registers_group_27_out));  // open: Selector
  _4_Registers_Group u_4_registers_group_28 (
    .CLK(CLK), .Data(undriven_22), .Enable(demultiplexer_2_out11), .Out(n4_registers_group_28_out));  // open: Selector
  _4_Registers_Group u_4_registers_group_29 (
    .CLK(CLK), .Data(undriven_22), .Enable(demultiplexer_2_out12), .Out(n4_registers_group_29_out));  // open: Selector
  _4_Registers_Group u_4_registers_group_30 (
    .CLK(CLK), .Data(undriven_22), .Enable(demultiplexer_2_out13), .Out(n4_registers_group_30_out));  // open: Selector
  _4_Registers_Group u_4_registers_group_31 (
    .CLK(CLK), .Data(undriven_22), .Enable(demultiplexer_2_out14), .Out(n4_registers_group_31_out));  // open: Selector
  _4_Registers_Group u_4_registers_group_32 (
    .CLK(CLK), .Data(undriven_22), .Enable(demultiplexer_2_out15), .Out(n4_registers_group_32_out));  // open: Selector
endmodule

module _4_Registers_Group (
  input  CLK,
  input  [7:0] Data,
  input  Enable,
  input  [1:0] Selector,
  output [31:0] Out
);

  wire demultiplexer_1_out0, demultiplexer_1_out1, demultiplexer_1_out2, demultiplexer_1_out3;

  Demultiplexer #(.select(2)) demultiplexer_1 (
    .out0(demultiplexer_1_out0), .out1(demultiplexer_1_out1), .out2(demultiplexer_1_out2),
    .out3(demultiplexer_1_out3), .in(Enable), .sel(Selector), .en(1'b1));
  Register register_1 (.D(Data), .en(demultiplexer_1_out0), .Q(Out[7:0]), .clk(CLK));  // open: clr
  Register register_2 (.D(Data), .en(demultiplexer_1_out1), .Q(Out[15:8]), .clk(CLK));  // open: clr
  Register register_3 (.D(Data), .en(demultiplexer_1_out2), .Q(Out[23:16]), .clk(CLK));  // open: clr
  Register register_4 (.D(Data), .en(demultiplexer_1_out3), .Q(Out[31:24]), .clk(CLK));  // open: clr
endmodule
